// Logisim project alu_circuit.circ as structural Verilog: 1 circuit, main circuit main
module main (
  input  in_1,
  input  in_2,
  input  in_3,
  input  in_4,
  input  in_5,
  input  in_6,
  input  in_7,
  input  in_8,
  input  in_9,
  input  in_10,
  input  in_11,
  input  in_12,
  input  in_13,
  input  in_14,
  output [7:0] out_15,
  output [7:0] out_16,
  output [7:0] out_17,
  output [7:0] out_18,
  output [7:0] out_19,
  output [7:0] out_20,
  output [7:0] out_21,
  output [7:0] out_22,
  output [7:0] out_23,
  output [7:0] out_24,
  output [7:0] out_25,
  output [7:0] out_26,
  output [7:0] out_27,
  output [7:0] out_28,
  output [7:0] out_29,
  output [3:0] out_30,
  output [3:0] out_31,
  output [2:0] out_32,
  output [7:0] out_33
);

  wire and_1_out, and_2_out, and_3_out, and_4_out, and_5_out, and_6_out, and_7_out, and_8_out, and_9_out,
       and_10_out, and_11_out, and_12_out, and_13_out, and_14_out, and_15_out, and_16_out, and_17_out,
       and_18_out, and_19_out, and_20_out, and_21_out, and_22_out, and_23_out, and_24_out, and_25_out,
       and_26_out, and_27_out, and_28_out, and_29_out, and_30_out, and_31_out, and_32_out, and_33_out,
       and_34_out, and_35_out, and_36_out, and_37_out, and_38_out, and_39_out, and_41_out, and_42_out,
       and_43_out, and_44_out, and_45_out, and_46_out, and_47_out, and_48_out, and_49_out, and_50_out,
       and_51_out, and_52_out, and_53_out, and_54_out, and_55_out, and_56_out, and_57_out, and_58_out,
       and_59_out, and_60_out, and_61_out, and_62_out, and_63_out, and_64_out, and_65_out, and_66_out,
       and_67_out, and_68_out, and_69_out, and_70_out, and_71_out, and_72_out, and_73_out, and_74_out,
       multiplexer_2_out, not_1_out, not_2_out, not_3_out, or_5_out, or_6_out, or_8_out, or_9_out, or_10_out,
       or_11_out, or_12_out, or_13_out, or_14_out, or_15_out, or_16_out, or_17_out, or_18_out, or_19_out,
       or_21_out, or_22_out, or_23_out, or_24_out, or_25_out, or_26_out, or_27_out, or_28_out, or_29_out,
       or_30_out, or_31_out, or_32_out, or_33_out, undriven, undriven_2, undriven_3, undriven_4, undriven_5,
       undriven_6, undriven_7, undriven_8, undriven_9, undriven_10, undriven_11, undriven_12, undriven_13,
       undriven_14, undriven_15, undriven_16, undriven_17, undriven_18, undriven_19, undriven_20,
       undriven_21, undriven_22, undriven_23, undriven_24, undriven_25, xor_5_out, xor_6_out, xor_8_out,
       xor_9_out, xor_10_out, xor_11_out, xor_12_out, xor_13_out, xor_14_out, xor_15_out, xor_17_out,
       xor_18_out, xor_19_out, xor_20_out, xor_21_out, xor_22_out, xor_23_out, xor_24_out, xor_26_out,
       xor_27_out, xor_28_out, xor_29_out, xor_30_out, xor_31_out, xor_35_out, xor_36_out, xor_37_out,
       xor_38_out, xor_39_out, xor_40_out, xor_42_out, xor_43_out, xor_44_out, xor_46_out, xor_48_out,
       xor_49_out, xor_51_out, xor_52_out, xor_53_out, xor_54_out, xor_55_out, xor_56_out, xor_57_out,
       xor_58_out, xor_59_out, xor_60_out, xor_61_out, xor_62_out, xor_63_out, xor_64_out, xor_65_out,
       xor_66_out, xor_67_out, xor_68_out, xor_69_out, xor_70_out, xor_71_out, xor_72_out, xor_73_out,
       xor_74_out, xor_75_out, xor_76_out, xor_77_out, xor_78_out, xor_79_out, xor_80_out, xor_81_out,
       xor_82_out;

  or or_1 (out_15[3], in_8, in_4);
  or or_2 (out_15[1], in_10, in_6);
  or or_3 (out_15[2], in_9, in_5);
  or or_4 (out_15[0], in_11, in_7);
  nand nand_1 (out_16[3], in_8, in_4);
  nand nand_2 (out_16[1], in_10, in_6);
  nand nand_3 (out_16[2], in_9, in_5);
  nand nand_4 (out_16[0], in_11, in_7);
  xor xor_1 (out_17[3], in_8, in_4);
  xor xor_2 (out_17[2], in_9, in_5);
  xor xor_3 (out_17[1], in_10, in_6);
  xor xor_4 (out_17[0], in_11, in_7);
  and and_1 (and_1_out, in_4, in_8);
  and and_2 (and_2_out, in_4, in_9);
  and and_3 (and_3_out, in_4, in_11);
  and and_4 (and_4_out, in_4, in_10);
  and and_5 (and_5_out, in_5, in_8);
  and and_6 (and_6_out, in_5, in_9);
  and and_7 (and_7_out, in_5, in_10);
  and and_8 (and_8_out, in_5, in_11);
  or or_5 (or_5_out, and_9_out, and_12_out);
  and and_9 (and_9_out, xor_8_out, or_8_out);
  xor xor_5 (xor_5_out, xor_8_out, or_8_out);
  or or_6 (or_6_out, and_10_out, and_13_out);
  and and_10 (and_10_out, xor_9_out, or_9_out);
  xor xor_6 (xor_6_out, xor_9_out, or_9_out);
  and and_11 (and_11_out, xor_10_out, or_10_out);
  or or_7 (out_21[7], and_11_out, and_14_out);
  xor xor_7 (out_21[6], xor_10_out, or_10_out);
  xor xor_8 (xor_8_out, xor_11_out, in_2);
  and and_12 (and_12_out, in_2, xor_11_out);
  xor xor_9 (xor_9_out, xor_12_out, or_5_out);
  and and_13 (and_13_out, or_5_out, xor_12_out);
  xor xor_10 (xor_10_out, xor_13_out, or_6_out);
  and and_14 (and_14_out, or_6_out, xor_13_out);
  xor xor_11 (xor_11_out, and_27_out, in_2);
  or or_8 (or_8_out, and_15_out, and_18_out);
  xor xor_12 (xor_12_out, and_5_out, in_2);
  or or_9 (or_9_out, and_16_out, and_19_out);
  xor xor_13 (xor_13_out, and_1_out, in_2);
  or or_10 (or_10_out, and_17_out, and_20_out);
  and and_15 (and_15_out, xor_17_out, or_11_out);
  xor xor_14 (xor_14_out, xor_17_out, or_11_out);
  and and_16 (and_16_out, xor_18_out, or_12_out);
  xor xor_15 (xor_15_out, xor_18_out, or_12_out);
  and and_17 (and_17_out, xor_19_out, or_13_out);
  xor xor_16 (out_21[5], xor_19_out, or_13_out);
  xor xor_17 (xor_17_out, xor_20_out, and_37_out);
  and and_18 (and_18_out, and_37_out, xor_20_out);
  xor xor_18 (xor_18_out, xor_21_out, xor_5_out);
  and and_19 (and_19_out, xor_5_out, xor_21_out);
  xor xor_19 (xor_19_out, xor_22_out, xor_6_out);
  and and_20 (and_20_out, xor_6_out, xor_22_out);
  xor xor_20 (xor_20_out, and_28_out, in_2);
  or or_11 (or_11_out, and_21_out, and_24_out);
  xor xor_21 (xor_21_out, and_6_out, in_2);
  or or_12 (or_12_out, and_22_out, and_25_out);
  xor xor_22 (xor_22_out, and_2_out, in_2);
  or or_13 (or_13_out, and_23_out, and_26_out);
  and and_21 (and_21_out, xor_27_out, or_14_out);
  xor xor_23 (xor_23_out, xor_27_out, or_14_out);
  and and_22 (and_22_out, xor_29_out, or_15_out);
  xor xor_24 (xor_24_out, xor_29_out, or_15_out);
  and and_23 (and_23_out, xor_31_out, or_16_out);
  xor xor_25 (out_21[4], xor_31_out, or_16_out);
  xor xor_26 (xor_26_out, and_29_out, in_2);
  xor xor_27 (xor_27_out, xor_26_out, and_38_out);
  and and_24 (and_24_out, and_38_out, xor_26_out);
  xor xor_28 (xor_28_out, and_7_out, in_2);
  xor xor_29 (xor_29_out, xor_28_out, xor_14_out);
  and and_25 (and_25_out, xor_14_out, xor_28_out);
  xor xor_30 (xor_30_out, and_4_out, in_2);
  xor xor_31 (xor_31_out, xor_30_out, xor_15_out);
  and and_26 (and_26_out, xor_15_out, xor_30_out);
  and and_27 (and_27_out, in_6, in_8);
  or or_14 (or_14_out, and_30_out, and_31_out);
  xor xor_32 (out_21[1], xor_35_out, in_2);
  or or_15 (or_15_out, and_32_out, and_33_out);
  xor xor_33 (out_21[2], xor_36_out, in_2);
  or or_16 (or_16_out, and_34_out, and_35_out);
  xor xor_34 (out_21[3], xor_37_out, in_2);
  and and_28 (and_28_out, in_6, in_9);
  and and_29 (and_29_out, in_6, in_10);
  xor xor_35 (xor_35_out, xor_38_out, and_39_out);
  and and_30 (and_30_out, xor_35_out, in_2);
  and and_31 (and_31_out, and_39_out, xor_38_out);
  and and_32 (and_32_out, xor_36_out, in_2);
  xor xor_36 (xor_36_out, xor_39_out, xor_23_out);
  and and_33 (and_33_out, xor_23_out, xor_39_out);
  xor xor_37 (xor_37_out, xor_40_out, xor_24_out);
  and and_34 (and_34_out, xor_37_out, in_2);
  and and_35 (and_35_out, xor_24_out, xor_40_out);
  and and_36 (and_36_out, in_6, in_11);
  xor xor_38 (xor_38_out, and_36_out, in_2);
  xor xor_39 (xor_39_out, and_8_out, in_2);
  xor xor_40 (xor_40_out, and_3_out, in_2);
  and and_37 (and_37_out, in_7, in_8);
  and and_38 (and_38_out, in_7, in_9);
  and and_39 (and_39_out, in_7, in_10);
  and and_40 (out_21[0], in_7, in_11);
  Multiplexer #(.select(3), .width(8)) multiplexer_1 (
    .in0({{4{in_2}}, out_15[3:0]}), .in1({{4{in_2}}, out_16[3:0]}), .in2({{4{in_2}}, out_17[3:0]}),
    .in3(out_21), .in4({{3{in_13}}, out_19[4:0]}), .in5({{3{in_13}}, out_19[4:0]}),
    .in6({{3{in_13}}, out_19[4:0]}), .in7({{5{in_2}}, in_4, in_5, in_6}), .out(out_33),
    .sel({in_12, in_13, in_14}));  // open: en
  or or_17 (or_17_out, and_41_out, and_42_out);
  and and_41 (and_41_out, xor_42_out, or_18_out);
  xor xor_41 (out_19[3], xor_42_out, or_18_out);
  xor xor_42 (xor_42_out, xor_43_out, in_4);
  and and_42 (and_42_out, in_4, xor_43_out);
  xor xor_43 (xor_43_out, and_48_out, in_13);
  or or_18 (or_18_out, and_43_out, and_44_out);
  xor xor_44 (xor_44_out, xor_46_out, in_5);
  and and_43 (and_43_out, xor_44_out, or_19_out);
  xor xor_45 (out_19[2], xor_44_out, or_19_out);
  and and_44 (and_44_out, in_5, xor_46_out);
  xor xor_46 (xor_46_out, and_51_out, in_13);
  or or_19 (or_19_out, and_45_out, and_46_out);
  and and_45 (and_45_out, xor_48_out, or_21_out);
  xor xor_47 (out_19[1], xor_48_out, or_21_out);
  xor xor_48 (xor_48_out, xor_49_out, in_6);
  and and_46 (and_46_out, in_6, xor_49_out);
  or or_20 (out_19[4], in_13, or_17_out);
  xor xor_49 (xor_49_out, and_50_out, in_13);
  and and_47 (and_47_out, xor_51_out, in_13);
  or or_21 (or_21_out, and_47_out, and_49_out);
  xor xor_50 (out_19[0], xor_51_out, in_13);
  and and_48 (and_48_out, in_8, multiplexer_2_out);
  xor xor_51 (xor_51_out, xor_52_out, in_7);
  and and_49 (and_49_out, in_7, xor_52_out);
  and and_50 (and_50_out, in_10, multiplexer_2_out);
  and and_51 (and_51_out, in_9, multiplexer_2_out);
  xor xor_52 (xor_52_out, or_22_out, in_13);
  not not_1 (not_1_out, in_11);
  Multiplexer multiplexer_2 (.in0(not_3_out), .in1(in_2), .out(multiplexer_2_out), .sel(in_14));  // open: en
  not not_2 (not_2_out, multiplexer_2_out);
  and and_52 (and_52_out, not_1_out, not_2_out);
  or or_22 (or_22_out, and_52_out, in_11);
  not not_3 (not_3_out, in_2);
  xor xor_53 (xor_53_out, in_1, undriven_2);
  xor xor_54 (xor_54_out, xor_53_out, undriven);
  and and_53 (and_53_out, xor_53_out, undriven);
  and and_54 (and_54_out, xor_54_out, in_1);
  xor xor_55 (xor_55_out, xor_54_out, in_1);
  or or_23 (or_23_out, and_55_out, and_56_out);
  or or_24 (or_24_out, and_54_out, and_53_out);
  and and_55 (and_55_out, xor_59_out, or_26_out);
  xor xor_56 (xor_56_out, xor_59_out, or_26_out);
  xor xor_57 (xor_57_out, in_1, undriven_4);
  xor xor_58 (xor_58_out, undriven_12, in_3);
  xor xor_59 (xor_59_out, xor_58_out, undriven_25);
  and and_56 (and_56_out, undriven_25, xor_58_out);
  xor xor_60 (xor_60_out, xor_57_out, undriven_3);
  and and_57 (and_57_out, xor_57_out, undriven_3);
  or or_25 (or_25_out, and_59_out, and_62_out);
  or or_26 (or_26_out, and_60_out, and_61_out);
  xor xor_61 (xor_61_out, xor_64_out, or_28_out);
  and and_58 (and_58_out, xor_60_out, or_24_out);
  xor xor_62 (xor_62_out, xor_60_out, or_24_out);
  and and_59 (and_59_out, xor_65_out, undriven_5);
  xor xor_63 (xor_63_out, xor_65_out, undriven_5);
  and and_60 (and_60_out, xor_64_out, or_28_out);
  xor xor_64 (xor_64_out, xor_66_out, undriven_6);
  and and_61 (and_61_out, undriven_6, xor_66_out);
  or or_27 (or_27_out, and_58_out, and_57_out);
  xor xor_65 (xor_65_out, undriven_8, undriven_9);
  and and_62 (and_62_out, undriven_9, undriven_8);
  xor xor_66 (xor_66_out, undriven_7, in_3);
  xor xor_67 (xor_67_out, in_1, undriven_11);
  or or_28 (or_28_out, and_63_out, and_65_out);
  and and_63 (and_63_out, xor_70_out, or_29_out);
  xor xor_68 (xor_68_out, xor_70_out, or_29_out);
  xor xor_69 (xor_69_out, xor_67_out, undriven_10);
  and and_64 (and_64_out, xor_67_out, undriven_10);
  xor xor_70 (xor_70_out, xor_73_out, undriven_20);
  and and_65 (and_65_out, undriven_20, xor_73_out);
  and and_66 (and_66_out, xor_69_out, or_27_out);
  xor xor_71 (xor_71_out, xor_69_out, or_27_out);
  xor xor_72 (xor_72_out, undriven_13, undriven_14);
  and and_67 (and_67_out, undriven_13, undriven_14);
  xor xor_73 (xor_73_out, undriven_15, in_3);
  or or_29 (or_29_out, and_70_out, and_72_out);
  or or_30 (or_30_out, and_66_out, and_64_out);
  xor xor_74 (xor_74_out, undriven_17, undriven_18);
  and and_68 (and_68_out, undriven_17, undriven_18);
  and and_69 (and_69_out, xor_72_out, undriven_19);
  xor xor_75 (xor_75_out, xor_72_out, undriven_19);
  and and_70 (and_70_out, xor_79_out, in_3);
  xor xor_76 (xor_76_out, xor_79_out, in_3);
  xor xor_77 (xor_77_out, in_1, undriven_24);
  xor xor_78 (xor_78_out, xor_74_out, undriven_21);
  and and_71 (and_71_out, xor_74_out, undriven_21);
  or or_31 (or_31_out, and_71_out, and_68_out);
  or or_32 (or_32_out, and_69_out, and_67_out);
  xor xor_79 (xor_79_out, xor_81_out, undriven_23);
  and and_72 (and_72_out, undriven_23, xor_81_out);
  xor xor_80 (xor_80_out, xor_77_out, undriven_22);
  and and_73 (and_73_out, xor_77_out, undriven_22);
  xor xor_81 (xor_81_out, undriven_16, in_3);
  and and_74 (and_74_out, xor_80_out, or_30_out);
  xor xor_82 (xor_82_out, xor_80_out, or_30_out);
  or or_33 (or_33_out, and_74_out, and_73_out);

  assign out_15[7:4] = {4{in_2}};
  assign out_16[7:4] = {4{in_2}};
  assign out_17[7:4] = {4{in_2}};
  assign out_18 = {{5{in_2}}, in_4, in_5, in_6};
  assign out_19[7:5] = {3{in_13}};
  assign out_22 = {{4{in_2}}, out_15[3:0]};
  assign out_23 = {{4{in_2}}, out_16[3:0]};
  assign out_24 = {{4{in_2}}, out_17[3:0]};
  assign out_25 = out_21;
  assign out_26 = {{3{in_13}}, out_19[4:0]};
  assign out_27 = {{3{in_13}}, out_19[4:0]};
  assign out_28 = {{3{in_13}}, out_19[4:0]};
  assign out_29 = {{5{in_2}}, in_4, in_5, in_6};
  assign out_30 = {in_4, in_5, in_6, in_7};
  assign out_31 = {in_8, in_9, in_10, in_11};
  assign out_32 = {in_12, in_13, in_14};
endmodule
